// Logisim project simplercpu.circ as structural Verilog: 1 circuit, main circuit main
module main (
);

  wire button_1_out, n7486_1_pin3, n7486_1_pin6, n7486_1_pin8, n7486_1_pin11, n74161_1_pin1, n74161_1_pin2,
       n74161_1_pin7, n74283_1_pin1, n74283_1_pin4, n74283_1_pin10, n74283_1_pin13, not_2_out;
  wire [3:0] n74157_1_pin4, n74161_1_pin14, register_1_q;
  wire [7:0] rom_1_data;

  _74161 #(.ShowInternalStructure("true")) u_74161_1 (
    .pin1(n74161_1_pin1), .pin2(n74161_1_pin2), .pin7(n74161_1_pin7), .pin14(n74161_1_pin14[0]),
    .pin13(n74161_1_pin14[1]), .pin12(n74161_1_pin14[2]), .pin11(n74161_1_pin14[3]), .pin10(n74161_1_pin7),
    .pin9(n74161_1_pin7));  // open: pin3, pin4, pin5, pin6, pin15
  Clock clock_1 (.out(n74161_1_pin2));
  not not_1 (n74161_1_pin1, button_1_out);
  Button button_1 (.out(button_1_out));
  Hex_Digit_Display hex_digit_display_1 (.value(n74161_1_pin14));  // open: dp
  ROM #(.addrWidth(15)) rom_1 (.addr({{11{1'b0}}, n74161_1_pin14}), .data(rom_1_data));
  Register #(.width(4)) register_1 (
    .D(rom_1_data[3:0]), .en(not_2_out), .clk(n74161_1_pin2), .Q(register_1_q));  // open: clr
  not not_2 (not_2_out, n74161_1_pin14[0]);
  _7486 #(.ShowInternalStructure("true")) u_7486_1 (
    .pin1(rom_1_data[1]), .pin2(rom_1_data[4]), .pin3(n7486_1_pin3), .pin4(rom_1_data[0]),
    .pin5(rom_1_data[4]), .pin6(n7486_1_pin6), .pin13(rom_1_data[3]), .pin12(rom_1_data[4]),
    .pin11(n7486_1_pin11), .pin10(rom_1_data[2]), .pin9(rom_1_data[4]), .pin8(n7486_1_pin8));
  _74283 #(.ShowInternalStructure("true")) u_74283_1 (
    .pin1(n74283_1_pin1), .pin2(register_1_q[1]), .pin3(n7486_1_pin3), .pin4(n74283_1_pin4),
    .pin5(n7486_1_pin6), .pin6(register_1_q[0]), .pin7(rom_1_data[4]), .pin15(register_1_q[2]),
    .pin14(n7486_1_pin8), .pin13(n74283_1_pin13), .pin12(n7486_1_pin11), .pin11(register_1_q[3]),
    .pin10(n74283_1_pin10));  // open: pin9
  _74157 #(.ShowInternalStructure("true")) u_74157_1 (
    .pin1(n74161_1_pin14[0]), .pin3(n74283_1_pin4), .pin4(n74157_1_pin4[0]), .pin6(n74283_1_pin1),
    .pin7(n74157_1_pin4[1]), .pin13(n74283_1_pin10), .pin12(n74157_1_pin4[3]), .pin10(n74283_1_pin13),
    .pin9(n74157_1_pin4[2]));  // open: pin2, pin5, pin15, pin14, pin11
  Hex_Digit_Display hex_digit_display_2 (.value(n74157_1_pin4));  // open: dp
  // also tied to VCC on the sheet: n74161_1_pin7

  // Notes on the sheet:
  //   contents of rom_1 (hex, n*v repeats v):
  //   f7 15
endmodule
